# Fritzing sketch BME280-Wiring (saved by Fritzing 0.9.4)
breadboards: 1

parts:
  U1 = NodeMCU V1.0
  Bauteil1 = BME280

nets:
  N1: U1.D1, Bauteil1.SCL
  N2: U1.D2, Bauteil1.SDA
  3V3: U1.3V3, Bauteil1.VIN
  GND: U1.GND, Bauteil1.GND

custom parts:
  NodeMCU V1.0: ESP8266 based NodeMCU
