# Fritzing sketch TFT-Wiring (saved by Fritzing 0.9.4)
breadboards: 2

parts:
  LCD1 = TFT 1.8 inch 160x128 w SD
  Bauteil1 = Breadboard Power Supply Board SMD
  U1 = ESP32-38PinWide [part_number=ESP32-38PinWide]

nets:
  N1: LCD1.pin_1, LCD1.pin_8, Bauteil1.VCC
  N2: LCD1.pin2, Bauteil1.GND
  N3: LCD1.pin3, U1.GPIO5
  N4: LCD1.pin4, U1.GPIO17
  N5: LCD1.pin_5, U1.GPIO16
  N6: LCD1.pin_6, U1.GPIO23
  N7: LCD1.pin_7, U1.GPIO18

notes:
  VCC: 5V
  VCC: 3.3V

custom parts:
  TFT 1.8 inch 160x128 w SD: This is a generic 1.8 tft spi lcd display available on ebay and others. The 1.8" display has 128x160 color pixels.
  ESP32-38PinWide: Generic 38-Pin ESP32 with wide format (only access to one side of pins on a breadboard) based on Stephen Lilley's HiLetgo ESP-WROOM-32 ESP32 ESP-32S Development Board.
